# Fritzing sketch MandoDistancia (saved by Fritzing 0.9.0b)
breadboards: 1

parts:
  Parte1 = Arduino Uno (Rev3)
  S1 = Pushbutton [package="[THT]"]
  S2 = Pushbutton [package="[THT]"]
  LED1 = LED - 5mm [color="Infrared (940nm)" package="5 mm [THT]"]
  IR1 = TSOP312.., 314.. [package=THT]
  R1 = Resistor [tolerance=±20% resistance=220 package=THT]
  R2 = Resistor [tolerance=±5% resistance=220 package=THT]
  R3 = Resistor [tolerance=±5% resistance=220 package=THT]

nets (from the schematic view):
  N1: Parte1.D11_PWM/MOSI, IR1.GND
  N2: Parte1.D2, R1.Pin_1
  N3: Parte1.D5_PWM, S2.Pin_1, S2.Pin_2, R2.Pin_0
  N4: Parte1.D6_PWM, S1.Pin_1, S1.Pin_2, R3.Pin_0
  N5: Parte1.5V, S1.Pin_3, S1.Pin_4, S2.Pin_3, S2.Pin_4, IR1.Data
  N6: Parte1.GND, LED1.cathode, IR1.Vs, R2.Pin_1, R3.Pin_1
  N7: LED1.anode, R1.Pin_0

notes:
  Librería IRremote
  Dos modos: recvDump y enviar
