# Fritzing sketch MandoDistanciaCompacto (saved by Fritzing 0.9.0b)
stripboards: 2

parts:
  Parte1 = Arduino Prototyping Shield
  S1 = Pushbutton [package="[THT]"]
  S2 = Pushbutton [package="[THT]"]
  R1 = Resistor [tolerance=±5% resistance=220 package=THT]
  R2 = Resistor [tolerance=±5% resistance=220 package=THT]
  LED1 = LED - 5mm [color="Red (633nm)" package="5 mm [THT]"]
  R3 = Resistor [tolerance=±5% resistance=220 package=THT]

nets:
  N1: Parte1.D5, S2.Pin_1, S2.Pin_2, R2.Pin_0
  N2: Parte1.D6, S1.Pin_3, S1.Pin_4, R1.Pin_1
  N3: Parte1.GND, R1.Pin_0, R2.Pin_1, LED1.cathode
  N4: Parte1.D3, R3.Pin_1
  N5: Parte1.+5V, S1.Pin_1, S1.Pin_2, S2.Pin_3, S2.Pin_4
  N6: LED1.anode, R3.Pin_0
